# Fritzing sketch Schematic (saved by Fritzing 0.9.3b)
breadboards: 1

parts:
  Part1 = FTDI Basic Programmer
  XTAL1 = Crystal [frequency="16 Mhz" package=THT]
  C2 = Ceramic Capacitor [capacitance=100nF package="100 mil [THT, multilayer]"]
  C3 = Capacitor [package=cap-pth-small2]
  C4 = Capacitor [package=cap-pth-small2]
  U1 = atmega328 [package=dip]
  DHT1 = DHT11 Humitidy and Temperature Sensor
  R1 = Resistor [tolerance=±5% resistance=10k package=THT]

nets:
  N1: Part1.DTR, C2.1
  N2: Part1.RXI, U1.D0_(RX)
  N3: Part1.TXO, U1.D1_(TX)
  VCC: Part1.POWER, U1.VCC, DHT1.VDD, R1.Pin_0
  GND: Part1.GND, C3.2, C4.1, U1.GND#7, DHT1.GND
  N4: XTAL1.pin_0, C4.2, U1.XLAT1
  N5: XTAL1.pin_1, C3.1, U1.XLAT2
  N6: C2.0, U1.RESET
  N7: U1.D13, DHT1.DATA, R1.Pin_1

custom parts:
  DHT11 Humitidy and Temperature Sensor: DHT11 Humidity and Temperature Sensor
